// Logisim project Cache(RAM).circ as structural Verilog: 2 circuits, main circuit main
module main (
  input  bit_7,
  input  bit_6,
  input  bit_5,
  input  bit_4,
  input  bit_3,
  input  bit_2,
  input  bit_1,
  input  bit_0,
  input  Read_0___Write_1,
  input  addr_3,
  input  addr_2,
  input  addr_1,
  input  addr_0,
  output bit_7_2,
  output bit_6_2,
  output bit_5_2,
  output bit_4_2,
  output bit_3_2,
  output bit_2_2,
  output bit_1_2,
  output bit_0_2,
  output [7:0] out_22,
  output [7:0] out_23
);

  wire and_1_out, and_2_out, and_3_out, and_4_out, and_6_out, and_7_out, and_8_out, and_9_out, and_10_out,
       and_11_out, and_12_out, and_13_out, and_14_out, and_15_out, and_16_out, and_17_out, and_18_out,
       and_19_out, and_20_out, and_21_out, and_22_out, and_23_out, and_24_out, and_25_out, and_26_out,
       and_27_out, and_28_out, and_29_out, and_30_out, and_31_out, and_32_out, and_33_out, and_34_out,
       and_35_out, and_36_out, and_37_out, and_38_out, and_39_out, and_40_out, and_41_out, and_42_out,
       and_43_out, and_44_out, and_45_out, and_46_out, and_47_out, and_48_out, and_49_out, and_50_out,
       and_51_out, and_52_out, and_53_out, and_54_out, and_55_out, and_56_out, and_57_out, and_58_out,
       and_59_out, and_60_out, and_61_out, and_62_out, and_63_out, and_64_out, and_65_out, and_66_out,
       and_67_out, and_68_out, and_69_out, and_70_out, and_71_out, and_72_out, and_73_out, and_74_out,
       and_75_out, and_76_out, and_77_out, and_78_out, and_79_out, and_80_out, and_81_out, and_82_out,
       and_83_out, and_84_out, and_85_out, and_86_out, and_87_out, and_88_out, not_1_out, not_2_out,
       not_3_out, not_4_out, not_5_out, not_6_out, not_7_out, not_8_out, not_9_out, not_10_out, not_11_out,
       not_12_out, not_13_out, not_14_out, not_15_out, not_16_out, not_17_out, not_18_out, not_19_out,
       not_20_out, not_21_out, not_22_out, not_23_out, not_24_out, not_25_out, not_26_out, not_27_out,
       not_28_out, not_29_out, not_30_out, not_31_out, not_32_out, not_33_out, not_34_out, not_35_out,
       not_36_out, not_37_out, not_38_out, not_39_out, not_40_out, not_41_out, not_42_out, not_43_out,
       not_44_out, not_45_out, not_46_out, not_47_out, not_48_out, not_49_out, not_50_out, not_51_out,
       not_52_out, not_53_out, not_54_out, not_55_out, not_56_out, not_57_out, not_58_out, not_59_out,
       not_60_out, not_61_out, not_62_out, not_63_out, not_64_out, not_65_out, not_66_out, not_67_out,
       not_68_out, not_69_out, or_1_out, or_2_out, or_3_out, or_4_out, or_5_out, or_6_out, or_7_out,
       or_8_out, or_9_out, or_10_out, or_11_out, or_12_out, or_13_out, or_14_out, Reset_out, s_r_ff_9_q,
       s_r_ff_10_q, s_r_ff_11_q, s_r_ff_12_q, s_r_ff_42_qn, Set_out;
  wire [7:0] readselector_1_off_bits, readselector_1_on_bits, readselector_2_off_bits,
       readselector_2_on_bits, readselector_3_on_bits, readselector_4_off_bits, readselector_4_on_bits,
       s_r_ff_20_q, s_r_ff_28_q, s_r_ff_36_q;

  not not_1 (not_1_out, s_r_ff_9_q);
  not not_2 (not_2_out, s_r_ff_10_q);
  not not_3 (not_3_out, s_r_ff_11_q);
  not not_4 (not_4_out, s_r_ff_12_q);
  not not_5 (not_5_out, s_r_ff_9_q);
  not not_6 (not_6_out, s_r_ff_10_q);
  not not_7 (not_7_out, s_r_ff_11_q);
  and and_1 (and_1_out, not_1_out, not_2_out, not_3_out, not_4_out, not_18_out);
  ReadSelector readselector_1 (
    .Input(s_r_ff_28_q), .R_W(and_2_out), .On_bits(readselector_1_on_bits), .Off_Bits(readselector_1_off_bits));
  and and_2 (and_2_out, not_5_out, not_6_out, not_7_out, s_r_ff_12_q, not_18_out);
  ReadSelector readselector_2 (
    .Input(s_r_ff_20_q), .R_W(and_1_out), .On_bits(readselector_2_on_bits), .Off_Bits(readselector_2_off_bits));
  not not_8 (not_8_out, s_r_ff_9_q);
  and and_3 (and_3_out, not_18_out, not_8_out, not_9_out, s_r_ff_11_q, s_r_ff_12_q);
  not not_9 (not_9_out, s_r_ff_10_q);
  not not_10 (not_10_out, s_r_ff_9_q);
  not not_11 (not_11_out, s_r_ff_10_q);
  not not_12 (not_12_out, s_r_ff_12_q);
  and and_4 (and_4_out, not_18_out, not_10_out, not_11_out, s_r_ff_11_q, not_12_out);
  ReadSelector readselector_3 (.Input(out_23), .R_W(and_3_out), .On_bits(readselector_3_on_bits), .Off_Bits(out_22));
  ReadSelector readselector_4 (
    .Input(s_r_ff_36_q), .R_W(and_4_out), .On_bits(readselector_4_on_bits), .Off_Bits(readselector_4_off_bits));
  // AND_Gate and_5 is placed but not wired
  and and_6 (and_6_out, not_13_out, Read_0___Write_1);
  or Reset (Reset_out, readselector_2_off_bits[7], readselector_1_off_bits[7], readselector_4_off_bits[7], and_6_out, out_22[7]);
  or or_1 (or_1_out, readselector_2_off_bits[6], readselector_1_off_bits[6], readselector_4_off_bits[6], and_7_out, out_22[7]);
  or or_2 (or_2_out, readselector_4_off_bits[5], and_8_out, readselector_1_off_bits[5], out_22[6]);
  or or_3 (or_3_out, readselector_2_off_bits[5], readselector_1_off_bits[4], readselector_4_off_bits[4], and_9_out, out_22[5]);
  or or_4 (or_4_out, readselector_2_off_bits[4], readselector_1_off_bits[3], readselector_4_off_bits[3], and_10_out, out_22[3], readselector_2_off_bits[3], out_22[4]);
  or or_5 (or_5_out, readselector_1_off_bits[2], readselector_4_off_bits[2], out_22[2], readselector_2_off_bits[2], and_11_out);
  or or_6 (or_6_out, readselector_2_off_bits[1], readselector_1_off_bits[1], readselector_4_off_bits[1], and_12_out, out_22[1]);
  or or_7 (or_7_out, readselector_2_off_bits[0], readselector_1_off_bits[0], readselector_4_off_bits[0], and_13_out, out_22[0]);
  and and_7 (and_7_out, not_23_out, Read_0___Write_1);
  and and_8 (and_8_out, not_24_out, Read_0___Write_1);
  and and_9 (and_9_out, not_25_out, Read_0___Write_1);
  and and_10 (and_10_out, not_34_out, Read_0___Write_1);
  and and_11 (and_11_out, not_35_out, Read_0___Write_1);
  or Set (Set_out, readselector_3_on_bits[7], readselector_2_on_bits[7], bit_7, readselector_4_on_bits[7], readselector_1_on_bits[7]);
  or or_8 (or_8_out, readselector_3_on_bits[6], readselector_2_on_bits[6], readselector_4_on_bits[6], readselector_1_on_bits[6], and_16_out);
  or or_9 (or_9_out, readselector_3_on_bits[5], readselector_2_on_bits[5], readselector_4_on_bits[5], readselector_1_on_bits[5], and_15_out);
  or or_10 (or_10_out, readselector_3_on_bits[4], readselector_2_on_bits[4], readselector_4_on_bits[4], readselector_1_on_bits[4], and_19_out);
  or or_11 (or_11_out, readselector_3_on_bits[3], readselector_2_on_bits[3], readselector_4_on_bits[3], readselector_1_on_bits[3], and_21_out);
  or or_12 (or_12_out, readselector_3_on_bits[2], readselector_2_on_bits[2], readselector_4_on_bits[2], readselector_1_on_bits[2], and_20_out);
  or or_13 (or_13_out, readselector_3_on_bits[1], readselector_2_on_bits[1], readselector_4_on_bits[1], readselector_1_on_bits[1], and_24_out);
  or or_14 (or_14_out, readselector_3_on_bits[0], readselector_2_on_bits[0], readselector_4_on_bits[0], readselector_1_on_bits[0], and_23_out);
  and and_12 (and_12_out, not_36_out, Read_0___Write_1);
  not not_13 (not_13_out, bit_7);
  and and_13 (and_13_out, not_37_out, Read_0___Write_1);
  S_R_Flip_Flop s_r_ff_1 (.Q(bit_7_2), .preset(Set_out), .reset(Reset_out));  // open: S, clk, R, Qn, en
  S_R_Flip_Flop s_r_ff_2 (.Q(bit_6_2), .preset(or_8_out), .reset(or_1_out));  // open: S, clk, R, Qn, en
  S_R_Flip_Flop s_r_ff_3 (.Q(bit_5_2), .preset(or_9_out), .reset(or_2_out));  // open: S, clk, R, Qn, en
  S_R_Flip_Flop s_r_ff_4 (.Q(bit_4_2), .preset(or_10_out), .reset(or_3_out));  // open: S, clk, R, Qn, en
  S_R_Flip_Flop s_r_ff_5 (.Q(bit_3_2), .preset(or_11_out), .reset(or_4_out));  // open: S, clk, R, Qn, en
  S_R_Flip_Flop s_r_ff_6 (.Q(bit_2_2), .preset(or_12_out), .reset(or_5_out));  // open: S, clk, R, Qn, en
  S_R_Flip_Flop s_r_ff_7 (.Q(bit_1_2), .preset(or_13_out), .reset(or_6_out));  // open: S, clk, R, Qn, en
  S_R_Flip_Flop s_r_ff_8 (.Q(bit_0_2), .preset(or_14_out), .reset(or_7_out));  // open: S, clk, R, Qn, en
  S_R_Flip_Flop s_r_ff_9 (.Q(s_r_ff_9_q), .preset(addr_3), .reset(not_14_out));  // open: S, clk, R, Qn, en
  not not_14 (not_14_out, addr_3);
  S_R_Flip_Flop s_r_ff_10 (.Q(s_r_ff_10_q), .preset(addr_2), .reset(not_15_out));  // open: S, clk, R, Qn, en
  not not_15 (not_15_out, addr_2);
  S_R_Flip_Flop s_r_ff_11 (.Q(s_r_ff_11_q), .preset(addr_1), .reset(not_16_out));  // open: S, clk, R, Qn, en
  not not_16 (not_16_out, addr_1);
  S_R_Flip_Flop s_r_ff_12 (.Q(s_r_ff_12_q), .preset(addr_0), .reset(not_17_out));  // open: S, clk, R, Qn, en
  not not_17 (not_17_out, addr_0);
  not not_18 (not_18_out, Read_0___Write_1);
  not not_19 (not_19_out, s_r_ff_9_q);
  and and_14 (and_14_out, Read_0___Write_1, not_19_out, not_20_out, not_21_out, not_22_out);
  not not_20 (not_20_out, s_r_ff_10_q);
  not not_21 (not_21_out, s_r_ff_11_q);
  not not_22 (not_22_out, s_r_ff_12_q);
  not not_23 (not_23_out, bit_6);
  not not_24 (not_24_out, bit_5);
  not not_25 (not_25_out, bit_4);
  and and_15 (and_15_out, bit_5, Read_0___Write_1);
  and and_16 (and_16_out, Read_0___Write_1, bit_6);
  not not_26 (not_26_out, s_r_ff_9_q);
  and and_17 (and_17_out, Read_0___Write_1, not_26_out, not_27_out, not_28_out, s_r_ff_12_q);
  not not_27 (not_27_out, s_r_ff_10_q);
  not not_28 (not_28_out, s_r_ff_11_q);
  not not_29 (not_29_out, s_r_ff_9_q);
  not not_30 (not_30_out, s_r_ff_10_q);
  and and_18 (and_18_out, Read_0___Write_1, not_29_out, not_30_out, s_r_ff_11_q, not_31_out);
  not not_31 (not_31_out, s_r_ff_12_q);
  not not_32 (not_32_out, s_r_ff_9_q);
  not not_33 (not_33_out, s_r_ff_10_q);
  not not_34 (not_34_out, bit_3);
  not not_35 (not_35_out, bit_2);
  not not_36 (not_36_out, bit_1);
  buf and_19 (and_19_out, bit_4);  // AND_Gate
  and and_20 (and_20_out, bit_2, Read_0___Write_1);
  and and_21 (and_21_out, Read_0___Write_1, bit_3);
  and and_22 (and_22_out, Read_0___Write_1, not_32_out, not_33_out, s_r_ff_11_q, s_r_ff_12_q);
  not not_37 (not_37_out, bit_0);
  and and_23 (and_23_out, bit_0, Read_0___Write_1);
  and and_24 (and_24_out, bit_1, Read_0___Write_1);
  and and_25 (and_25_out, bit_7_2, and_14_out);
  and and_26 (and_26_out, and_14_out, not_38_out);
  not not_38 (not_38_out, bit_7_2);
  and and_27 (and_27_out, bit_6_2, and_14_out);
  and and_28 (and_28_out, and_14_out, not_39_out);
  not not_39 (not_39_out, bit_6_2);
  and and_29 (and_29_out, bit_5_2, and_14_out);
  and and_30 (and_30_out, and_14_out, not_40_out);
  not not_40 (not_40_out, bit_5_2);
  and and_31 (and_31_out, bit_4_2, and_14_out);
  and and_32 (and_32_out, and_14_out, not_41_out);
  not not_41 (not_41_out, bit_4_2);
  and and_33 (and_33_out, bit_3_2, and_14_out);
  and and_34 (and_34_out, and_14_out, not_42_out);
  not not_42 (not_42_out, bit_3_2);
  and and_35 (and_35_out, bit_2_2, and_14_out);
  and and_36 (and_36_out, and_14_out, not_43_out);
  not not_43 (not_43_out, bit_2_2);
  and and_37 (and_37_out, bit_1_2, and_14_out);
  and and_38 (and_38_out, and_14_out, not_44_out);
  not not_44 (not_44_out, bit_1_2);
  and and_39 (and_39_out, bit_0_2, and_14_out);
  and and_40 (and_40_out, and_14_out, not_45_out);
  not not_45 (not_45_out, bit_0_2);
  and and_41 (and_41_out, bit_7_2, and_17_out);
  and and_42 (and_42_out, and_17_out, not_46_out);
  not not_46 (not_46_out, bit_7_2);
  and and_43 (and_43_out, bit_6_2, and_17_out);
  and and_44 (and_44_out, and_17_out, not_47_out);
  not not_47 (not_47_out, bit_6_2);
  and and_45 (and_45_out, bit_5_2, and_17_out);
  and and_46 (and_46_out, and_17_out, not_48_out);
  not not_48 (not_48_out, bit_5_2);
  and and_47 (and_47_out, bit_4_2, and_17_out);
  and and_48 (and_48_out, and_17_out, not_49_out);
  not not_49 (not_49_out, bit_4_2);
  and and_49 (and_49_out, bit_3_2, and_17_out);
  and and_50 (and_50_out, and_17_out, not_50_out);
  not not_50 (not_50_out, bit_3_2);
  and and_51 (and_51_out, bit_2_2, and_17_out);
  and and_52 (and_52_out, and_17_out, not_51_out);
  not not_51 (not_51_out, bit_2_2);
  and and_53 (and_53_out, bit_1_2, and_17_out);
  and and_54 (and_54_out, and_17_out, not_52_out);
  not not_52 (not_52_out, bit_1_2);
  and and_55 (and_55_out, bit_0_2, and_17_out);
  and and_56 (and_56_out, and_17_out, not_53_out);
  not not_53 (not_53_out, bit_0_2);
  and and_57 (and_57_out, bit_7_2, and_18_out);
  and and_58 (and_58_out, and_18_out, not_54_out);
  not not_54 (not_54_out, bit_7_2);
  and and_59 (and_59_out, bit_6_2, and_18_out);
  and and_60 (and_60_out, and_18_out, not_55_out);
  not not_55 (not_55_out, bit_6_2);
  and and_61 (and_61_out, bit_5_2, and_18_out);
  and and_62 (and_62_out, and_18_out, not_56_out);
  not not_56 (not_56_out, bit_5_2);
  and and_63 (and_63_out, bit_4_2, and_18_out);
  and and_64 (and_64_out, and_18_out, not_57_out);
  not not_57 (not_57_out, bit_4_2);
  and and_65 (and_65_out, bit_3_2, and_18_out);
  and and_66 (and_66_out, and_18_out, not_58_out);
  not not_58 (not_58_out, bit_3_2);
  and and_67 (and_67_out, bit_2_2, and_18_out);
  and and_68 (and_68_out, and_18_out, not_59_out);
  not not_59 (not_59_out, bit_2_2);
  and and_69 (and_69_out, bit_1_2, and_18_out);
  and and_70 (and_70_out, and_18_out, not_60_out);
  not not_60 (not_60_out, bit_1_2);
  and and_71 (and_71_out, bit_0_2, and_18_out);
  and and_72 (and_72_out, and_18_out, not_61_out);
  not not_61 (not_61_out, bit_0_2);
  and and_73 (and_73_out, bit_7_2, and_22_out);
  not not_62 (not_62_out, bit_7_2);
  and and_74 (and_74_out, bit_6_2, and_22_out);
  not not_63 (not_63_out, bit_6_2);
  and and_75 (and_75_out, bit_5_2, and_22_out);
  not not_64 (not_64_out, bit_5_2);
  and and_76 (and_76_out, bit_4_2, and_22_out);
  not not_65 (not_65_out, bit_4_2);
  and and_77 (and_77_out, bit_3_2, and_22_out);
  not not_66 (not_66_out, bit_3_2);
  and and_78 (and_78_out, bit_2_2, and_22_out);
  not not_67 (not_67_out, bit_2_2);
  and and_79 (and_79_out, bit_1_2, and_22_out);
  not not_68 (not_68_out, bit_1_2);
  and and_80 (and_80_out, bit_0_2, and_22_out);
  not not_69 (not_69_out, bit_0_2);
  and and_81 (and_81_out, and_22_out, not_62_out);
  and and_82 (and_82_out, and_22_out, not_63_out);
  and and_83 (and_83_out, and_22_out, not_64_out);
  and and_84 (and_84_out, and_22_out, not_65_out);
  and and_85 (and_85_out, and_22_out, not_66_out);
  and and_86 (and_86_out, and_22_out, not_67_out);
  and and_87 (and_87_out, and_22_out, not_68_out);
  and and_88 (and_88_out, and_22_out, not_69_out);
  S_R_Flip_Flop s_r_ff_13 (.Q(s_r_ff_20_q[7]), .preset(and_25_out), .reset(and_26_out));  // open: S, clk, R, Qn, en
  S_R_Flip_Flop s_r_ff_14 (.Q(s_r_ff_20_q[6]), .preset(and_27_out), .reset(and_28_out));  // open: S, clk, R, Qn, en
  S_R_Flip_Flop s_r_ff_15 (.Q(s_r_ff_20_q[5]), .preset(and_29_out), .reset(and_30_out));  // open: S, clk, R, Qn, en
  S_R_Flip_Flop s_r_ff_16 (.Q(s_r_ff_20_q[4]), .preset(and_31_out), .reset(and_32_out));  // open: S, clk, R, Qn, en
  S_R_Flip_Flop s_r_ff_17 (.Q(s_r_ff_20_q[3]), .preset(and_33_out), .reset(and_34_out));  // open: S, clk, R, Qn, en
  S_R_Flip_Flop s_r_ff_18 (.Q(s_r_ff_20_q[2]), .preset(and_35_out), .reset(and_36_out));  // open: S, clk, R, Qn, en
  S_R_Flip_Flop s_r_ff_19 (.Q(s_r_ff_20_q[1]), .preset(and_37_out), .reset(and_38_out));  // open: S, clk, R, Qn, en
  S_R_Flip_Flop s_r_ff_20 (.Q(s_r_ff_20_q[0]), .preset(and_39_out), .reset(and_40_out));  // open: S, clk, R, Qn, en
  S_R_Flip_Flop s_r_ff_21 (.Q(s_r_ff_28_q[7]), .preset(and_41_out), .reset(and_42_out));  // open: S, clk, R, Qn, en
  S_R_Flip_Flop s_r_ff_22 (.Q(s_r_ff_28_q[6]), .preset(and_43_out), .reset(and_44_out));  // open: S, clk, R, Qn, en
  S_R_Flip_Flop s_r_ff_23 (.Q(s_r_ff_28_q[5]), .preset(and_45_out), .reset(and_46_out));  // open: S, clk, R, Qn, en
  S_R_Flip_Flop s_r_ff_24 (.Q(s_r_ff_28_q[4]), .preset(and_47_out), .reset(and_48_out));  // open: S, clk, R, Qn, en
  S_R_Flip_Flop s_r_ff_25 (.Q(s_r_ff_28_q[3]), .preset(and_49_out), .reset(and_50_out));  // open: S, clk, R, Qn, en
  S_R_Flip_Flop s_r_ff_26 (.Q(s_r_ff_28_q[2]), .preset(and_51_out), .reset(and_52_out));  // open: S, clk, R, Qn, en
  S_R_Flip_Flop s_r_ff_27 (.Q(s_r_ff_28_q[1]), .preset(and_53_out), .reset(and_54_out));  // open: S, clk, R, Qn, en
  S_R_Flip_Flop s_r_ff_28 (.Q(s_r_ff_28_q[0]), .preset(and_55_out), .reset(and_56_out));  // open: S, clk, R, Qn, en
  S_R_Flip_Flop s_r_ff_29 (.Q(s_r_ff_36_q[7]), .preset(and_57_out), .reset(and_58_out));  // open: S, clk, R, Qn, en
  S_R_Flip_Flop s_r_ff_30 (.Q(s_r_ff_36_q[6]), .preset(and_59_out), .reset(and_60_out));  // open: S, clk, R, Qn, en
  S_R_Flip_Flop s_r_ff_31 (.Q(s_r_ff_36_q[5]), .preset(and_61_out), .reset(and_62_out));  // open: S, clk, R, Qn, en
  S_R_Flip_Flop s_r_ff_32 (.Q(s_r_ff_36_q[4]), .preset(and_63_out), .reset(and_64_out));  // open: S, clk, R, Qn, en
  S_R_Flip_Flop s_r_ff_33 (.Q(s_r_ff_36_q[3]), .preset(and_65_out), .reset(and_66_out));  // open: S, clk, R, Qn, en
  S_R_Flip_Flop s_r_ff_34 (.Q(s_r_ff_36_q[2]), .preset(and_67_out), .reset(and_68_out));  // open: S, clk, R, Qn, en
  S_R_Flip_Flop s_r_ff_35 (.Q(s_r_ff_36_q[1]), .preset(and_69_out), .reset(and_70_out));  // open: S, clk, R, Qn, en
  S_R_Flip_Flop s_r_ff_36 (.Q(s_r_ff_36_q[0]), .preset(and_71_out), .reset(and_72_out));  // open: S, clk, R, Qn, en
  S_R_Flip_Flop s_r_ff_37 (.Q(out_23[7]), .preset(and_73_out), .reset(and_81_out));  // open: S, clk, R, Qn, en
  S_R_Flip_Flop s_r_ff_38 (.Q(out_23[6]), .preset(and_74_out), .reset(and_82_out));  // open: S, clk, R, Qn, en
  S_R_Flip_Flop s_r_ff_39 (.Q(out_23[5]), .preset(and_75_out), .reset(and_83_out));  // open: S, clk, R, Qn, en
  S_R_Flip_Flop s_r_ff_40 (.Q(out_23[4]), .preset(and_76_out), .reset(and_84_out));  // open: S, clk, R, Qn, en
  S_R_Flip_Flop s_r_ff_41 (.Q(out_23[3]), .preset(and_77_out), .reset(and_85_out));  // open: S, clk, R, Qn, en
  S_R_Flip_Flop s_r_ff_42 (
    .Q(out_23[2]), .Qn(s_r_ff_42_qn), .preset(and_78_out), .reset(and_86_out));  // open: S, clk, R, en
  S_R_Flip_Flop s_r_ff_43 (.Q(out_23[1]), .preset(and_79_out), .reset(and_87_out));  // open: S, clk, R, Qn, en
  S_R_Flip_Flop s_r_ff_44 (.Q(out_23[0]), .preset(and_80_out), .reset(and_88_out));  // open: S, clk, R, Qn, en
  // NOT_Gate not_70 is placed but not wired

  // Notes on the sheet:
  //   Data Register
  //   Address register
endmodule

module ReadSelector (
  input  [7:0] Input,
  input  R_W,
  output [7:0] On_bits,
  output [7:0] Off_Bits
);

  wire not_1_out, not_2_out, not_3_out, not_4_out, not_5_out, not_6_out, not_7_out, not_8_out;

  and and_1 (On_bits[0], Input[0], R_W);
  and and_2 (On_bits[1], Input[1], R_W);
  and and_3 (On_bits[2], Input[2], R_W);
  and and_4 (On_bits[3], Input[3], R_W);
  and and_5 (On_bits[4], R_W, Input[4]);
  and and_6 (On_bits[5], Input[5], R_W);
  and and_7 (On_bits[6], Input[6], R_W);
  and and_8 (On_bits[7], Input[7], R_W);
  not not_1 (not_1_out, On_bits[1]);
  not not_2 (not_2_out, On_bits[0]);
  not not_3 (not_3_out, On_bits[2]);
  not not_4 (not_4_out, On_bits[3]);
  not not_5 (not_5_out, On_bits[4]);
  not not_6 (not_6_out, On_bits[5]);
  not not_7 (not_7_out, On_bits[6]);
  not not_8 (not_8_out, On_bits[7]);
  and and_9 (Off_Bits[0], not_2_out, R_W);
  and and_10 (Off_Bits[1], not_1_out, R_W);
  and and_11 (Off_Bits[2], not_3_out, R_W);
  and and_12 (Off_Bits[3], not_4_out, R_W);
  and and_13 (Off_Bits[4], not_5_out, R_W);
  and and_14 (Off_Bits[5], not_6_out, R_W);
  and and_15 (Off_Bits[6], R_W, not_7_out);
  and and_16 (Off_Bits[7], R_W, not_8_out);
endmodule
